# Fritzing sketch magnet-sensor (saved by Fritzing 0.9.6b)
breadboards: 1

parts:
  S1 = Magnetic Door Switch [package=reed_switch_plastic]
  R1 = Resistor [tolerance=±5% resistance=220 package="0805 [SMD]"]
  U2 = ESP8266 NodeMCU LoLin module

nets:
  N1: S1.1, U2.3V3
  N2: S1.2, R1.Pin_0, U2.D1
  N3: R1.Pin_1, U2.GND

custom parts:
  ESP8266 NodeMCU LoLin module: ESP8266 based NodeMCU
